# Fritzing sketch dotmatrix (saved by Fritzing 0.9.3b)
breadboards: 2

parts:
  Part1 = Arduino Uno (Rev3) - ICSP
  LED_Dot_Matrix = LBT2088AH [part_number=LBT2088AH]
  R1 = Resistor [tolerance=±5% resistance=220 package="0402 [SMD]"]  # not connected
  R2 = Resistor [tolerance=±5% resistance=220 package="0402 [SMD]"]  # not connected
  R3 = Resistor [tolerance=±5% resistance=220 package="0402 [SMD]"]  # not connected
  R4 = Resistor [tolerance=±5% resistance=220 package="0402 [SMD]"]  # not connected
  R5 = Resistor [tolerance=±5% resistance=220 package="0402 [SMD]"]  # not connected
  R6 = Resistor [tolerance=±5% resistance=220 package="0402 [SMD]"]  # not connected
  R7 = Resistor [tolerance=±5% resistance=220 package="0402 [SMD]"]  # not connected
  R8 = Resistor [tolerance=±5% resistance=220 package="0402 [SMD]"]

nets:
  N1: Part1.A4/SDA, LED_Dot_Matrix.pin_12
  N2: Part1.A5/SCL, LED_Dot_Matrix.pin_8
  N3: Part1.D9_PWM, R8.Pin_1
  N4: Part1.D0/RX, LED_Dot_Matrix.pin_9
  N5: Part1.D4, LED_Dot_Matrix.pin_14
